# Fritzing sketch Ac-vent-filter (saved by Fritzing 0.9.3b)
perfboards: 4

parts:
  U2 = LCD-16X2 [package=lcd-16x2]  # not connected
  C2 = Electrolytic Capacitor [capacitance=1µF package="100 mil [THT, electrolytic]"]  # not connected
  RHT2 = Humidity and Temperature Sensor RHT03  # not connected
  J2 = Basic Servo
  Part4 = Arduino Uno (Rev3)
  S7 = Taiway 100-SP-X-T1 SPDT Miniature Toggle Switch [part_number=100-SP-X-T1-0-0-B1-M2 package=THT]  # not connected
  S8 = Pushbutton [package="[THT]"]
  S9 = Pushbutton [package="[THT]"]
  R7 = Resistor [tolerance=±5% resistance=220 package="2512 [SMD]"]  # not connected
  RHT3 = Humidity and Temperature Sensor RHT03  # not connected
  R9 = Resistor [tolerance=±5% resistance=220 package="2512 [SMD]"]  # not connected
  R10 = Resistor [tolerance=±5% resistance=220 package="2512 [SMD]"]  # not connected

nets:
  N1: J2.pulse, Part4.D13/SCK
  N2: S8.Pin_1, S8.Pin_2
  N3: S8.Pin_3, S8.Pin_4
  N4: S9.Pin_1, S9.Pin_2
  N5: S9.Pin_3, S9.Pin_4

// code stored in the sketch: ac-cover.ino

